# Fritzing sketch Music_piano_graph (saved by Fritzing 0.9.3b)
breadboards: 1

parts:
  Raspberry_Pi_1 = Raspberry Pi 3 [part_number=RPI-3-V1.2]
  R1 = 330 Ω Resistor [package=THT]
  R2 = 330 Ω Resistor [package=THT]
  R3 = 330 Ω Resistor [package=THT]
  R6 = 330 Ω Resistor [package=THT]
  White = LED - 5mm [color="White (6500K)" package="5 mm [THT]"]
  Yellow = LED - 5mm [color="Yellow (595nm)" package="5 mm [THT]"]
  Red = LED - 5mm [color="Red (633nm)" package="5 mm [THT]"]
  Blue = LED - 5mm [color="Blue (525nm)" package="5 mm [THT]"]
  Green = LED - 5mm [color="Green (570nm)" package="5 mm [THT]"]
  Snow = LED - 5mm [color="White (6500K)" package="5 mm [THT]"]
  S1 = Pushbutton [package="[THT]"]
  S2 = Pushbutton [package="[THT]"]
  S3 = Pushbutton [package="[THT]"]
  S4 = Pushbutton [package="[THT]"]
  S5 = Pushbutton [package="[THT]"]
  S6 = Pushbutton [package="[THT]"]
  S7 = Pushbutton [package="[THT]"]
  S8 = Pushbutton [package="[THT]"]
  R4 = 330 Ω Resistor [package=THT]
  R5 = 330 Ω Resistor [package=THT]

nets:
  N1: Raspberry_Pi_1.GPIO17, S8.Pin_3, S8.Pin_4
  N2: Raspberry_Pi_1.GPIO27, S7.Pin_3, S7.Pin_4
  N3: Raspberry_Pi_1.GPIO22, S6.Pin_3, S6.Pin_4
  N4: Raspberry_Pi_1.GND, R1.Pin_0, R2.Pin_0, R6.Pin_0, S1.Pin_3, S1.Pin_4, S2.Pin_3, S2.Pin_4, S3.Pin_3, S3.Pin_4, S4.Pin_3, S4.Pin_4, S5.Pin_1, S5.Pin_2, S6.Pin_1, S6.Pin_2, S7.Pin_1, S7.Pin_2, S8.Pin_1, S8.Pin_2, R4.Pin_0, R5.Pin_0
  N5: Raspberry_Pi_1.GPIO5, S4.Pin_1, S4.Pin_2
  N6: Raspberry_Pi_1.GPIO6, S3.Pin_1, S3.Pin_2
  N7: Raspberry_Pi_1.GPIO13, S5.Pin_3, S5.Pin_4
  N8: Raspberry_Pi_1.GPIO19, S2.Pin_1, S2.Pin_2
  N9: Raspberry_Pi_1.GPIO21, White.anode
  N10: Raspberry_Pi_1.GPIO20, S1.Pin_1, S1.Pin_2
  N11: Raspberry_Pi_1.GPIO16, Yellow.anode
  N12: Raspberry_Pi_1.GPIO12, Red.anode
  N13: Raspberry_Pi_1.GPIO25, Blue.anode
  N14: Raspberry_Pi_1.GPIO24, Green.anode
  N15: Raspberry_Pi_1.GPIO23, Snow.anode
  N16: R1.Pin_1, White.cathode
  N17: R2.Pin_1, Yellow.cathode
  N18: R3.Pin_1, Red.cathode
  N19: R6.Pin_1, Snow.cathode
  N20: Blue.cathode, R4.Pin_1
  N21: Green.cathode, R5.Pin_1

custom parts:
  330 Ω Resistor: A generic 5-band resistor (0.25W)
